# Fritzing sketch SpectrumAnalyzer (saved by Fritzing 0.3.16b)

parts:
  LCD1 = LCD screen
  R1 = Resistor [resistance=4.7k package=THT]
  R2 = Resistor [resistance=15k package=THT]
  R1_2 = Resistor [resistance=4.7k package=THT]
  R2_2 = Resistor [resistance=15k package=THT]
  R1_3 = Resistor [resistance=4.7k package=THT]
  R2_3 = Resistor [resistance=15k package=THT]
  R1_4 = Resistor [resistance=4.7k package=THT]
  R1_5 = Resistor [resistance=4.7k package=THT]
  C1 = Electrolytic Capacitor [package=THT]
  R2_4 = Resistor [resistance=15k package=THT]
  R2_5 = Resistor [resistance=15k package=THT]
  Arduino1 = Arduino Nano v2.3
  U1 = mystery part, 8 pins [chip_label=CYWM6935 spacing=300mil]
  R3 = Resistor [resistance=6.8k package=THT]
  R1_6 = Resistor [resistance=4.7k package=THT]
  R1_7 = Resistor [resistance=4.7k package=THT]
  R1_8 = Resistor [resistance=4.7k package=THT]
  R2_6 = Resistor [resistance=15k package=THT]
  R2_7 = Resistor [resistance=15k package=THT]
  R2_8 = Resistor [resistance=15k package=THT]
  S1 = Pushbutton [package="[THT]"]
  R4 = Resistor [resistance=15k package=THT]
  R5 = Resistor [resistance=4.7k package=THT]
  J1 = Piezo Speaker

nets:
  N1: LCD1.DB2, R1_5.Pin_0, R2_5.Pin_0
  N2: LCD1.DB3, C1.+
  N3: LCD1.DB4, R2.Pin_1, R2_2.Pin_1, R2_3.Pin_1, C1.-, R2_4.Pin_1, R2_5.Pin_1, Arduino1.GND, U1.pin8, R2_6.Pin_0, R2_7.Pin_0, R2_8.Pin_0, R4.Pin_0
  N4: LCD1.DB5, R1_4.Pin_0, R2_4.Pin_0
  N5: LCD1.DB6, R2.Pin_0, R1_3.Pin_0
  N6: LCD1.DB7, R1_2.Pin_0, R2_2.Pin_0, U1.pin6
  N7: LCD1.LED+, R1.Pin_0, R2_3.Pin_0, U1.pin4
  N8: LCD1.LED-, Arduino1.3V3, U1.pin1, R3.Pin_1
  N9: R1.Pin_1, Arduino1.D13
  N10: R1_2.Pin_1, Arduino1.D11
  N11: R1_3.Pin_1, Arduino1.D9
  N12: R1_4.Pin_1, Arduino1.D7
  N13: R1_5.Pin_1, Arduino1.D8
  N14: Arduino1.D3, J1.pin1
  N15: Arduino1.D4, R1_7.Pin_1
  N16: Arduino1.D5, R1_6.Pin_1
  N17: Arduino1.D6, R5.Pin_1
  N18: Arduino1.D12, R1_8.Pin_1
  N19: Arduino1.+5V, S1.Pin_3, S1.Pin_4, J1.pin2
  N20: U1.pin2, R1_6.Pin_0, R2_8.Pin_1
  N21: U1.pin3, R1_7.Pin_0, R2_7.Pin_1
  N22: U1.pin5, R1_8.Pin_0, R2_6.Pin_1
  N23: U1.pin7, R3.Pin_0
  N24: S1.Pin_1, S1.Pin_2, R4.Pin_1, R5.Pin_0
